# Fritzing sketch Untitled Sketch 2 (saved by Fritzing 0.9.3b)
breadboards: 1

parts:
  Part1 = Arduino Uno (Rev3) - ICSP
  WeMos_D1_R1 = WeMos D1 R2
  S1 = H-Bridge with L298N
  Propeller_motor = DC Motor
  Steering_motor = DC Motor
  5_V = BATTERY-2 [package=battery-aa]
  5_V_2 = BATTERY-2 [package=battery-aa]
  R2 = Resistor [tolerance=±5% resistance=1k package="1206 [SMD]"]
  R1 = Resistor [tolerance=±5% resistance=2.2k package="2010 [SMD]"]

nets:
  N1: Part1.D9_PWM, S1.ENB
  N2: Part1.D10_PWM/SS, WeMos_D1_R1.D15
  N3: Part1.D11_PWM/MOSI, R2.Pin_0
  N4: Part1.D3_PWM, S1.IN1
  N5: Part1.D4, S1.IN2
  N6: Part1.D5_PWM, S1.ENA
  N7: Part1.D6_PWM, S1.IN3
  N8: Part1.D7, S1.IN4
  N9: Part1.5V, 5_V.+1, 5_V_2.-1
  GND: Part1.GND, S1.GND, 5_V.-1
  N10: WeMos_D1_R1.D14, R2.Pin_1, R1.Pin_0
  N11: S1.12V, 5_V_2.+1
  N12: S1.M1-01, Steering_motor.pin_2
  N13: S1.M1-02, Steering_motor.pin_1
  N14: S1.M2-01, Propeller_motor.pin_2
  N15: S1.M2-02, Propeller_motor.pin_1

custom parts:
  WeMos D1 R2: The D1 R2 is a mini wifi board based on the ESP-8266EX.
  H-Bridge with L298N: h-bridge
